# Fritzing sketch StopwatchGame (saved by Fritzing 0.9.5d)
breadboards: 1

parts:
  Part1 = Arduino Mega 2560 (Rev3)
  R4 = Resistor [tolerance=±5% resistance=220 package=THT]
  R5 = Resistor [tolerance=±5% resistance=220 package=THT]
  R6 = Resistor [tolerance=±5% resistance=220 package=THT]
  R7 = Resistor [tolerance=±5% resistance=220 package=THT]
  LED1 = LED - 5mm [color="Red (633nm)" package="5 mm [THT]"]
  LED2 = LED - 5mm [color="Red (633nm)" package="5 mm [THT]"]
  LED3 = LED - 5mm [color="Red (633nm)" package="5 mm [THT]"]
  LED4 = LED - 5mm [color="Green (555nm)" package="5 mm [THT]"]
  U1 = 7-Segment-Display-4-Red [part_number=HS420561K package="7-Segment-4 [THT]"]
  R8 = Resistor [tolerance=±5% resistance=1k package=THT]
  R9 = Resistor [tolerance=±5% resistance=1k package=THT]
  R10 = Resistor [tolerance=±5% resistance=1k package=THT]
  R11 = Resistor [tolerance=±5% resistance=1k package=THT]
  S2 = Pushbutton [package="[SMD]"]

nets:
  N1: Part1.D13_PWM, S2.Pin_3, S2.Pin_4
  N2: Part1.D12_PWM, R10.Pin_1
  N3: Part1.D11_PWM, U1.pin_11
  N4: Part1.D10_PWM, U1.pin_10
  N5: Part1.D9_PWM, R11.Pin_1
  N6: Part1.D8_PWM, R8.Pin_1
  N7: Part1.D1_TX0, U1.pin1
  N8: Part1.D2_PWM, U1.pin2
  N9: Part1.D3_PWM, U1.pin3
  N10: Part1.D4_PWM, U1.pin4
  N11: Part1.D5_PWM, U1.pin5
  N12: Part1.D6_PWM, R9.Pin_1
  N13: Part1.D7_PWM, U1.pin7
  N14: Part1.D46, R7.Pin_1
  N15: Part1.D48, R6.Pin_1
  N16: Part1.D50, R4.Pin_1
  N17: Part1.D52, R5.Pin_1
  N18: Part1.GND, LED1.anode, LED2.anode, LED3.anode, LED4.anode, S2.Pin_1, S2.Pin_2
  N19: R4.Pin_0, LED3.cathode
  N20: R5.Pin_0, LED4.cathode
  N21: R6.Pin_0, LED2.cathode
  N22: R7.Pin_0, LED1.cathode
  N23: U1.pin6, R9.Pin_0
  N24: U1.pin8, R8.Pin_0
  N25: U1.pin_9, R11.Pin_0
  N26: U1.pin_12, R10.Pin_0

custom parts:
  7-Segment-Display-4-Red: 7-Segment Display 4 digits Red
